// Digital circuit bf_2.dig as structural Verilog
module bf_2 (
  input  clk
);

  wire _16x20b_ram_input_selector_1_c, _16x20b_ram_input_selector_1_ld, _16x20b_ram_input_selector_1_str,
       and_1_out, and_2_out, and_3_out, and_6_out, and_7_out, and_8_out, comparator_1_eq, comparator_2_eq,
       comparator_3_eq, delay_1_out, delay_2_out, delay_3_out, delay_4_out, delay_5_out, delay_6_out, EOF,
       EOF_2_eq, EOF_eq, not_1_out, not_2_out, not_3_out, not_4_out, one_time_bit_1_clk_2,
       one_time_bit_1_rst, or_1_out, or_3_out, or_4_out, or_5_out, or_6_out, or_7_out, RLE_opcodes_d,
       RLEcompress, WHILEaddresses;
  wire [3:0] opc_transl_d;
  wire [7:0] counterpreset_1_out, original_BF_program_d, prev_opc_q, xor_1_out;
  wire [15:0] _16x20b_ram_input_selector_1_a, counter_1_out, loops_d, multiplexer_1_out, PC_out, PPC_out,
       sub_1_s;
  wire [19:0] _16x20b_ram_input_selector_1_d, RLE_program_d;

  not not_1 (not_1_out, RLEcompress);
  Counter #(.Bits(16)) PPC (.en(1'b1), .C(not_1_out), .clr(1'b0), .out(PPC_out));  // open: ovf
  Sub #(.Bits(16)) sub_1 (.a(PPC_out), .b(16'h1), .c_i(1'b0), .s(sub_1_s));  // open: c_o
  RAMDualPort #(.AddrBits(16), .isProgramMemory("true"), .Bits(8)) original_BF_program (
    .A(sub_1_s), .Din({8{1'b0}}), .str(1'b0), .C(1'b0), .ld(1'b1), .D(original_BF_program_d));
  Register #(.Bits(8)) prev_opc (.D(original_BF_program_d), .C(RLEcompress), .en(1'b1), .Q(prev_opc_q));
  assign xor_1_out = original_BF_program_d ^ prev_opc_q;  // XOr xor_1, 8 bits wide
  ROM #(.AddrBits(8), .Bits(4)) opc_transl (.A(prev_opc_q), .sel(1'b1), .D(opc_transl_d));
  ROM #(.AddrBits(8)) RLE_opcodes (.A(prev_opc_q), .sel(not_1_out), .D(RLE_opcodes_d));
  or or_1 (or_1_out, xor_1_out[0], xor_1_out[1], xor_1_out[2], xor_1_out[3], xor_1_out[4], xor_1_out[5], xor_1_out[6], xor_1_out[7]);
  PullDown pulldown_1 (.out(RLE_opcodes_d));
  Delay #(.delayTime(3)) delay_1 (.in(RLEcompress), .out(delay_1_out));
  Comparator #(.Bits(8)) u_EOF (.a({8{1'b0}}), .b(original_BF_program_d), .eq(EOF_eq));  // open: gt, lt
  Comparator #(.Bits(4)) comparator_1 (.a(4'b0000), .b(opc_transl_d), .eq(comparator_1_eq));  // open: gt, lt
  Comparator #(.Bits(4)) comparator_2 (.a(opc_transl_d), .b(4'b0101), .eq(comparator_2_eq));  // open: gt, lt
  Comparator #(.Bits(4)) comparator_3 (.a(opc_transl_d), .b(4'b0110), .eq(comparator_3_eq));  // open: gt, lt
  and and_1 (and_1_out, RLEcompress, EOF_eq);
  not not_2 (not_2_out, comparator_1_eq);
  not not_3 (not_3_out, EOF);
  or or_2 (EOF, EOF, and_1_out);
  and and_2 (and_2_out, comparator_2_eq, delay_1_out);
  and and_3 (and_3_out, delay_1_out, comparator_3_eq);
  or or_3 (or_3_out, or_1_out, RLE_opcodes_d);
  not not_4 (not_4_out, or_1_out);
  and and_4 (RLEcompress, not_3_out, clk);
  and and_5 (WHILEaddresses, clk, EOF);
  and and_6 (and_6_out, or_3_out, not_2_out);
  and and_7 (and_7_out, not_2_out, not_4_out, RLEcompress);
  or or_4 (or_4_out, and_2_out, and_3_out);
  or or_5 (or_5_out, and_7_out, or_1_out);
  Delay delay_2 (.in(or_5_out), .out(delay_2_out));
  Counter #(.Bits(16)) counter_1 (.en(and_7_out), .C(delay_2_out), .clr(or_1_out), .out(counter_1_out));  // open: ovf
  CounterPreset #(.Bits(8)) counterpreset_1 (
    .en(or_4_out), .C(or_4_out), .dir(and_3_out), .in({8{1'b0}}), .ld(1'b0), .clr(1'b0),
    .out(counterpreset_1_out));  // open: ovf
  one_time_bit one_time_bit_1 (.Clk(WHILEaddresses), .Rst(one_time_bit_1_rst), .Clk_2(one_time_bit_1_clk_2));
  or or_6 (or_6_out, one_time_bit_1_clk_2, and_6_out);
  RAMDualPort #(.AddrBits(8), .Bits(16)) loops (
    .A(counterpreset_1_out), .Din(PC_out), .str(1'b1), .C(and_2_out), .ld(1'b1), .D(loops_d));
  Break break_1 (.brk(one_time_bit_1_rst));
  Delay #(.delayTime(3)) delay_3 (.in(one_time_bit_1_rst), .out(delay_3_out));
  or or_7 (or_7_out, or_6_out, delay_3_out);
  Multiplexer #(.Bits(16)) multiplexer_1 (
    .sel(and_3_out), .in_0(counter_1_out), .in_1(loops_d), .out(multiplexer_1_out));
  Delay #(.delayTime(5)) delay_4 (.in(and_3_out), .out(delay_4_out));
  CounterPreset #(.Bits(16)) PC (
    .en(or_6_out), .C(or_7_out), .dir(delay_3_out), .in({16{1'b0}}), .ld(1'b0), .clr(1'b0), .out(PC_out));  // open: ovf
  Delay delay_5 (.in(delay_4_out), .out(delay_5_out));
  _16x20b_ram_input_selector _16x20b_ram_input_selector_1 (
    .A1(PC_out), .D1({multiplexer_1_out, opc_transl_d}), .str1(1'b1), .C1(and_6_out), .ld1(1'b1),
    .Go2(delay_4_out), .A2(loops_d), .D2({PC_out, 4'b0101}), .str2(delay_4_out), .C2(delay_5_out),
    .ld2(1'b1), .A(_16x20b_ram_input_selector_1_a), .D(_16x20b_ram_input_selector_1_d),
    .str(_16x20b_ram_input_selector_1_str), .C(_16x20b_ram_input_selector_1_c),
    .ld(_16x20b_ram_input_selector_1_ld));
  RAMDualPort #(.AddrBits(16), .Bits(20)) RLE_program (
    .A(_16x20b_ram_input_selector_1_a), .Din(_16x20b_ram_input_selector_1_d),
    .str(_16x20b_ram_input_selector_1_str), .C(_16x20b_ram_input_selector_1_c),
    .ld(_16x20b_ram_input_selector_1_ld), .D(RLE_program_d));
  Comparator #(.Bits(4)) EOF_2 (.a(4'b0000), .b(RLE_program_d[3:0]), .eq(EOF_2_eq));  // open: gt, lt
  Delay #(.delayTime(4)) delay_6 (.in(one_time_bit_1_clk_2), .out(delay_6_out));
  and and_8 (and_8_out, delay_6_out, EOF_2_eq);
  Break break_2 (.brk(and_8_out));

  // Notes on the sheet:
  //   clk: Hz: 1000000
  //   ASCII reminder
  //   0x2B +
  //   0x2D -
  //   0x3E >
  //   0x3C <
  //   0x5B [
  //   0x5D ]
  //   0x2E .
  //   0x2C ,
  //   0x23 #
  //   current
  //   opcode
  //   contents of opc_transl (hex, n*v repeats v):
  //   0,0,0,0,0,0,0,0,0,0,0,0,0,0,0,0,0,0,0,0,0,0,0,0,0,0,0,0,0,0,0,0,0,0,0,0,0,0,0,0,0,
  //   0,0,1,8,2,7,0,0,0,0,0,0,0,0,0,0,0,0,0,4,0,3,0,0,0,0,0,0,0,0,0,0,0,0,0,0,0,0,0,0,0,
  //   0,0,0,0,0,0,0,0,0,5,0,6
  //   contents of RLE_opcodes (hex, n*v repeats v):
  //   0,0,0,0,0,0,0,0,0,0,0,0,0,0,0,0,0,0,0,0,0,0,0,0,0,0,0,0,0,0,0,0,0,0,0,0,0,0,0,0,0,
  //   0,0,a,1,0,1,0,0,0,0,0,0,0,0,0,0,0,0,0,0,0,0,0,0,0,0,0,0,0,0,0,0,0,0,0,0,0,0,0,0,0,
  //   0,0,0,0,0,0,0,0,0,1,0,1
  //   clocks goes to CPU when compressor reaches EOF
  //   opc != old
  //   opc changed
  //   old is valid
  //   old is not RLE
  //   old is [
  //   old is ]
  //   write down
  //   Inc or Clear
  //   have to happen after opcode has been written
  //   thus the delay
  //   old opcode
  //   count
  //   back address
  //   RLE Compressor
  //   quantity, ignored for non-RLE opcodes
  //   opcode
endmodule
