// Digital circuit bf_cpu_standalone.dig as structural Verilog
module bf_cpu_standalone (
  input  clk,
  output [7:0] Chr,
  output Out,
  output Stop
);

  wire _16x20b_ram_input_selector_1_c, _16x20b_ram_input_selector_1_ld, _16x20b_ram_input_selector_1_str,
       _16x20b_ram_input_selector_2_c, _16x20b_ram_input_selector_2_ld, _16x20b_ram_input_selector_2_str,
       and_1_out, and_2_out, and_3_out, and_4_out, and_7_out, and_8_out, and_9_out, and_10_out, and_12_out,
       and_13_out, comparator_1_eq, comparator_2_eq, comparator_3_eq, comparator_4_eq, comparator_5_eq,
       comparator_6_eq, comparator_7_eq, comparator_7_lt, Compressor, CPU, decoder_1_out_0, decoder_1_out_1,
       decoder_1_out_2, decoder_1_out_3, decoder_1_out_4, decoder_1_out_5, decoder_1_out_6, decoder_1_out_8,
       decoder_1_out_9, decoder_1_out_10, decoder_1_out_11, decoder_1_out_12, decoder_1_out_13,
       decoder_1_out_14, decoder_1_out_15, delay_1_out, delay_2_out, delay_3_out, delay_4_out, delay_5_out,
       delay_6_out, delay_7_out, EOF, EOF_eq, not_1_out, not_2_out, not_3_out, not_4_out, not_5_out,
       not_6_out, not_7_out, opc_is_inverse_d, or_1_out, or_2_out, or_4_out, or_5_out, or_6_out, or_7_out,
       or_8_out, or_9_out, RLE_opcodes_d;
  wire [3:0] multiplexer_1_out, opc_transl_d;
  wire [7:0] add_2_s, counterpreset_1_out, multiplexer_4_out, opc__2_q, opc__3_q, original_BF_program_d,
       prev_opc_q, xor_1_out;
  wire [15:0] _16x20b_ram_input_selector_1_a, _16x20b_ram_input_selector_2_a, add_1_s, counter_1_out,
       loops_d, mem_ptr_out, multiplexer_2_out, multiplexer_3_out, neg_1_out, PC_out, PPC_out, RLE_PC_out,
       sub_1_s;
  wire [19:0] _16x20b_ram_input_selector_1_d, _16x20b_ram_input_selector_2_d, RLE_program_d;

  not not_1 (not_1_out, Compressor);
  Counter #(.Bits(16)) PPC (.en(1'b1), .C(not_1_out), .clr(1'b0), .out(PPC_out));  // open: ovf
  Sub #(.Bits(16)) sub_1 (.a(PPC_out), .b(16'h1), .c_i(1'b0), .s(sub_1_s));  // open: c_o
  Register #(.Bits(8)) opc__2 (.D(prev_opc_q), .C(Compressor), .en(1'b1), .Q(opc__2_q));
  Register #(.Bits(8)) opc__3 (.D(opc__2_q), .C(Compressor), .en(1'b1), .Q(opc__3_q));
  RAMDualPort #(.AddrBits(16), .isProgramMemory("true"), .Bits(8)) original_BF_program (
    .A(sub_1_s), .Din({8{1'b0}}), .str(1'b0), .C(1'b0), .ld(1'b1), .D(original_BF_program_d));
  Comparator #(.Bits(8)) comparator_1 (.a(prev_opc_q), .b(8'h5d), .eq(comparator_1_eq));  // open: gt, lt
  Comparator #(.Bits(8)) comparator_2 (.a(opc__2_q), .b(8'h2d), .eq(comparator_2_eq));  // open: gt, lt
  Comparator #(.Bits(8)) comparator_3 (.a(opc__3_q), .b(8'h5b), .eq(comparator_3_eq));  // open: gt, lt
  Register #(.Bits(8)) prev_opc (.D(original_BF_program_d), .C(Compressor), .en(1'b1), .Q(prev_opc_q));
  and and_1 (and_1_out, comparator_1_eq, comparator_2_eq, comparator_3_eq);
  assign xor_1_out = original_BF_program_d ^ prev_opc_q;  // XOr xor_1, 8 bits wide
  ROM #(.AddrBits(8), .Bits(4)) opc_transl (.A(prev_opc_q), .sel(1'b1), .D(opc_transl_d));
  ROM #(.AddrBits(8)) RLE_opcodes (.A(prev_opc_q), .sel(not_1_out), .D(RLE_opcodes_d));
  ROM #(.AddrBits(8)) opc_is_inverse (.A(prev_opc_q), .sel(1'b1), .D(opc_is_inverse_d));
  or or_1 (or_1_out, xor_1_out[0], xor_1_out[1], xor_1_out[2], xor_1_out[3], xor_1_out[4], xor_1_out[5], xor_1_out[6], xor_1_out[7]);
  PullDown pulldown_1 (.out(RLE_opcodes_d));
  Delay #(.delayTime(3)) delay_1 (.in(Compressor), .out(delay_1_out));
  or or_2 (or_2_out, Stop, or_2_out);
  Comparator #(.Bits(8)) u_EOF (.a({8{1'b0}}), .b(original_BF_program_d), .eq(EOF_eq));  // open: gt, lt
  Comparator #(.Bits(4)) comparator_4 (.a(4'b0000), .b(opc_transl_d), .eq(comparator_4_eq));  // open: gt, lt
  Comparator #(.Bits(4)) comparator_5 (.a(opc_transl_d), .b(4'b0110), .eq(comparator_5_eq));  // open: gt, lt
  Comparator #(.Bits(4)) comparator_6 (.a(opc_transl_d), .b(4'b0101), .eq(comparator_6_eq));  // open: gt, lt
  not not_2 (not_2_out, or_2_out);
  Break break_1 (.brk(or_2_out));
  and and_2 (and_2_out, Compressor, EOF_eq);
  not not_3 (not_3_out, comparator_4_eq);
  or or_3 (EOF, EOF, and_2_out);
  and and_3 (and_3_out, comparator_6_eq, delay_1_out);
  and and_4 (and_4_out, delay_1_out, comparator_5_eq);
  not not_4 (not_4_out, EOF);
  or or_4 (or_4_out, or_1_out, RLE_opcodes_d);
  not not_5 (not_5_out, or_1_out);
  and and_5 (Compressor, not_4_out, not_2_out, clk);
  and and_6 (CPU, clk, not_2_out, EOF);
  and and_7 (and_7_out, or_4_out, not_3_out);
  and and_8 (and_8_out, not_3_out, not_5_out, Compressor);
  or or_5 (or_5_out, and_3_out, and_4_out);
  or or_6 (or_6_out, and_8_out, or_1_out);
  Multiplexer #(.Bits(4)) multiplexer_1 (.sel(and_1_out), .in_0(opc_transl_d), .in_1(4'b1001), .out(multiplexer_1_out));
  Delay delay_2 (.in(or_6_out), .out(delay_2_out));
  Counter #(.Bits(16)) counter_1 (.en(and_8_out), .C(delay_2_out), .clr(or_1_out), .out(counter_1_out));  // open: ovf
  CounterPreset #(.Bits(8)) counterpreset_1 (
    .en(or_5_out), .C(or_5_out), .dir(and_4_out), .in({8{1'b0}}), .ld(1'b0), .clr(1'b0),
    .out(counterpreset_1_out));  // open: ovf
  Neg #(.Bits(16)) neg_1 (.in(counter_1_out), .out(neg_1_out));
  RAMDualPort #(.AddrBits(8), .Bits(16)) loops (
    .A(counterpreset_1_out), .Din(RLE_PC_out), .str(1'b1), .C(and_3_out), .ld(1'b1), .D(loops_d));
  Multiplexer #(.Bits(16)) multiplexer_2 (
    .sel(opc_is_inverse_d), .in_0(counter_1_out), .in_1(neg_1_out), .out(multiplexer_2_out));
  Delay #(.delayTime(2)) delay_3 (.in(and_7_out), .out(delay_3_out));
  Multiplexer #(.Bits(16)) multiplexer_3 (
    .sel(comparator_5_eq), .in_0(multiplexer_2_out), .in_1(loops_d), .out(multiplexer_3_out));
  Delay #(.delayTime(3)) delay_4 (.in(CPU), .out(delay_4_out));
  not not_6 (not_6_out, CPU);
  Counter #(.Bits(16)) RLE_PC (.en(delay_3_out), .C(delay_3_out), .clr(1'b0), .out(RLE_PC_out));  // open: ovf
  Delay #(.delayTime(3)) delay_5 (.in(and_4_out), .out(delay_5_out));
  and and_9 (and_9_out, delay_4_out, not_6_out);
  and and_10 (and_10_out, delay_5_out, and_4_out);
  or or_7 (or_7_out, and_9_out, or_8_out);
  Delay delay_6 (.in(and_10_out), .out(delay_6_out));
  CounterPreset #(.Bits(16)) PC (
    .en(and_9_out), .C(or_7_out), .dir(1'b0), .in(RLE_program_d[19:4]), .ld(or_8_out), .clr(1'b0),
    .out(PC_out));  // open: ovf
  _16x20b_ram_input_selector _16x20b_ram_input_selector_1 (
    .A1(RLE_PC_out), .D1({multiplexer_3_out, multiplexer_1_out}), .str1(1'b1), .C1(and_7_out), .ld1(1'b0),
    .Go2(and_10_out), .A2(loops_d), .D2({RLE_PC_out, 4'b0101}), .str2(and_10_out), .C2(delay_6_out),
    .ld2(1'b0), .A(_16x20b_ram_input_selector_1_a), .D(_16x20b_ram_input_selector_1_d),
    .str(_16x20b_ram_input_selector_1_str), .C(_16x20b_ram_input_selector_1_c),
    .ld(_16x20b_ram_input_selector_1_ld));
  not not_7 (not_7_out, EOF);
  _16x20b_ram_input_selector _16x20b_ram_input_selector_2 (
    .A1(PC_out), .D1({20{1'b0}}), .str1(1'b0), .C1(1'b0), .ld1(CPU), .Go2(not_7_out),
    .A2(_16x20b_ram_input_selector_1_a), .D2(_16x20b_ram_input_selector_1_d),
    .str2(_16x20b_ram_input_selector_1_str), .C2(_16x20b_ram_input_selector_1_c),
    .ld2(_16x20b_ram_input_selector_1_ld), .A(_16x20b_ram_input_selector_2_a),
    .D(_16x20b_ram_input_selector_2_d), .str(_16x20b_ram_input_selector_2_str),
    .C(_16x20b_ram_input_selector_2_c), .ld(_16x20b_ram_input_selector_2_ld));
  RAMDualPort #(.AddrBits(16), .Bits(20)) RLE_program (
    .A(_16x20b_ram_input_selector_2_a), .Din(_16x20b_ram_input_selector_2_d),
    .str(_16x20b_ram_input_selector_2_str), .C(_16x20b_ram_input_selector_2_c),
    .ld(_16x20b_ram_input_selector_2_ld), .D(RLE_program_d));
  Delay #(.delayTime(5)) delay_7 (.in(CPU), .out(delay_7_out));
  Decoder #(.Selector_Bits(4)) decoder_1 (
    .sel(RLE_program_d[3:0]), .out_0(decoder_1_out_0), .out_1(decoder_1_out_1), .out_2(decoder_1_out_2),
    .out_3(decoder_1_out_3), .out_4(decoder_1_out_4), .out_5(decoder_1_out_5), .out_6(decoder_1_out_6),
    .out_7(Out), .out_8(decoder_1_out_8), .out_9(decoder_1_out_9), .out_10(decoder_1_out_10),
    .out_11(decoder_1_out_11), .out_12(decoder_1_out_12), .out_13(decoder_1_out_13),
    .out_14(decoder_1_out_14), .out_15(decoder_1_out_15));
  and and_11 (Stop, delay_7_out, decoder_1_out_0);
  PullUp #(.Bits(4)) pullup_1 (.out(RLE_program_d[3:0]));
  or or_8 (or_8_out, and_13_out, and_12_out);
  and and_12 (and_12_out, decoder_1_out_6, comparator_7_lt);
  and and_13 (and_13_out, decoder_1_out_5, comparator_7_eq);
  Comparator #(.Bits(8)) comparator_7 (.a({8{1'b0}}), .b(Chr), .eq(comparator_7_eq), .lt(comparator_7_lt));  // open: gt
  CounterPreset #(.Bits(16)) mem_ptr (
    .en(1'b0), .C(decoder_1_out_3), .dir(1'b0), .in(add_1_s), .ld(decoder_1_out_3), .clr(1'b0),
    .out(mem_ptr_out));  // open: ovf
  Add #(.Bits(16)) add_1 (.a(mem_ptr_out), .b(RLE_program_d[19:4]), .c_i(1'b0), .s(add_1_s));  // open: c_o
  Multiplexer #(.Bits(8)) multiplexer_4 (
    .sel(decoder_1_out_9), .in_0(add_2_s), .in_1({8{1'b0}}), .out(multiplexer_4_out));
  or or_9 (or_9_out, decoder_1_out_9, decoder_1_out_1);
  RAMDualPort #(.AddrBits(16), .Bits(8)) RAM (
    .A(mem_ptr_out), .Din(multiplexer_4_out), .str(1'b1), .C(or_9_out), .ld(1'b1), .D(Chr));
  Add #(.Bits(8)) add_2 (.a(Chr), .b(RLE_program_d[11:4]), .c_i(1'b0), .s(add_2_s));  // open: c_o
  Terminal #(.termWidth(132), .termHeight(50)) terminal_1 (.D(Chr), .C(Out), .en(1'b1));

  // Other names for the same wires on the sheet: EOP = Stop

  // Notes on the sheet:
  //   clk: Hz: 1000000000
  //   ASCII reminder
  //   0x2B +
  //   0x2D -
  //   0x3E >
  //   0x3C <
  //   0x5B [
  //   0x5D ]
  //   0x2E .
  //   0x2C ,
  //   0x23 #
  //   current
  //   opcode
  //   RLE Compressor
  //   contents of opc_transl (hex, n*v repeats v):
  //   0,0,0,0,0,0,0,0,0,0,0,0,0,0,0,0,0,0,0,0,0,0,0,0,0,0,0,0,0,0,0,0,0,0,0,0,0,0,0,0,0,
  //   0,0,1,8,1,7,0,0,0,0,0,0,0,0,0,0,0,0,0,3,0,3,0,0,0,0,0,0,0,0,0,0,0,0,0,0,0,0,0,0,0,
  //   0,0,0,0,0,0,0,0,0,5,0,6
  //   contents of RLE_opcodes (hex, n*v repeats v):
  //   0,0,0,0,0,0,0,0,0,0,0,0,0,0,0,0,0,0,0,0,0,0,0,0,0,0,0,0,0,0,0,0,0,0,0,0,0,0,0,0,0,
  //   0,0,a,1,0,1,0,0,0,0,0,0,0,0,0,0,0,0,0,0,0,0,0,0,0,0,0,0,0,0,0,0,0,0,0,0,0,0,0,0,0,
  //   0,0,0,0,0,0,0,0,0,1,0,1
  //   contents of opc_is_inverse (hex, n*v repeats v):
  //   0,0,0,0,0,0,0,0,0,0,0,0,0,0,0,0,0,0,0,0,0,0,0,0,0,0,0,0,0,0,0,0,0,0,0,0,0,0,0,0,0,
  //   0,0,0,8,1,0,0,0,0,0,0,0,0,0,0,0,0,0,0,1,0,0,0,0,0,0,0,0,0,0,0,0,0,0,0,0,0,0,0,0,0,
  //   0,0,0,0,0,0,0,0,0,0,0,6
  //   clocks goes to CPU when compressor reaches EOF
  //   opc != old
  //   JMPs resolution
  //   opc changed
  //   old is valid
  //   old is not RLE
  //   old is [
  //   old is ]
  //   old opcode
  //   withour - or <
  //   write down
  //   Inc or Clear
  //   have to happen after opcode has been written
  //   thus the delay
  //   count
  //   back address
  //   BF CPU
  //   Qty or JPM address
  //   opcode
  //   +
  //   -
  //   >
  //   <
  //   [
  //   ]
  //   .
  //   ,
  //   Z
endmodule
