// Digital circuit 8b_or.dig as structural Verilog
module _8b_or (
  input  [7:0] \byte ,
  output \or 
);

  or or_1 (\or , \byte [0], \byte [1], \byte [2], \byte [3], \byte [4], \byte [5], \byte [6], \byte [7]);
endmodule
